// Logisim project Monociclo.circ as structural Verilog: 9 circuits, main circuit main
module main (
  input  in_1
);

  wire ALUSrc, and_1_out, and_2_out, and_3_out, Branch, Jal, Jr, Jump, MemRead, MemToReg, MemWrite,
       not_1_out, not_2_out, RegDest, RegWrite, Reloj, Salir, Zero;
  wire [1:0] ALUOp;
  wire [2:0] alu_control_1_op;
  wire [4:0] multiplexer_1_out, multiplexer_2_out;
  wire [5:0] Func;
  wire [31:0] adder_2_out, alu_1_aluresult, multiplexer_3_out, multiplexer_4_out, multiplexer_5_out,
       multiplexer_6_out, multiplexer_7_out, PC, PC_q, ram_1_dout, RegWriteData, T2, WriteData;
  wire [31:6] T1;
  wire [31:16] T3;
  wire [31:26] rom_1_data;

  not not_1 (not_1_out, Salir);
  Register #(.width(32)) u_PC (.D(multiplexer_6_out), .clk(and_1_out), .Q(PC_q), .clr(in_1));  // open: en
  and and_1 (and_1_out, Reloj, not_1_out);
  ROM #(.addrWidth(24), .dataWidth(32)) rom_1 (
    .addr(PC_q[23:0]), .data({rom_1_data, T3[31], T3[24:16], T1[31], T1[14:6], Func}));
  Adder #(.width(32)) adder_1 (.a(PC_q), .b(32'h1), .out(PC));  // open: cin, cout
  Multiplexer #(.enable("false"), .width(5)) multiplexer_1 (
    .in0(T3[20:16]), .in1({T1[31], T1[14:11]}), .out(multiplexer_1_out), .sel(RegDest));
  Adder #(.width(32)) adder_2 (.a(PC), .b({{17{T1[31]}}, T1[14:6], Func}), .out(adder_2_out));  // open: cin, cout
  and and_2 (and_2_out, Branch, Zero);
  Alu_Con_Op alu_con_op_1 (
    .Opcode(rom_1_data), .salir(Salir), .RegDest(RegDest), .Jump(Jump), .ALUSrc(ALUSrc),
    .MemtonReg(MemToReg), .RegWrite(RegWrite), .MemRead(MemRead), .MemWrite(MemWrite), .Branch(Branch),
    .Jal(Jal), .ALUOp(ALUOp));
  Multiplexer #(.enable("false"), .width(5)) multiplexer_2 (
    .in0(multiplexer_1_out), .in1({5{1'b1}}), .out(multiplexer_2_out), .sel(Jal));
  Clock clock_1 (.out(Reloj));
  Multiplexer #(.enable("false"), .width(32)) multiplexer_3 (
    .in0(PC), .in1(adder_2_out), .out(multiplexer_3_out), .sel(and_2_out));
  Multiplexer #(.enable("false"), .width(32)) multiplexer_4 (
    .in0(multiplexer_3_out), .in1({{7{T3[31]}}, T3[24:16], T1[31], T1[14:6], Func}), .out(multiplexer_4_out),
    .sel(Jump));
  Multiplexer #(.enable("false"), .width(32)) multiplexer_5 (
    .in0(RegWriteData), .in1(PC), .out(multiplexer_5_out), .sel(Jal));
  Multiplexer #(.enable("false"), .width(32)) multiplexer_6 (
    .in0(multiplexer_4_out), .in1(T2), .out(multiplexer_6_out), .sel(Jr));
  Reg_File reg_file_1 (
    .Read_Register_1({T3[31], T3[24:21]}), .RegWrite(RegWrite), .Write_Reg(multiplexer_2_out),
    .Write_Data(multiplexer_5_out), .Clock(Reloj), .Reset(in_1), .Read_Register_2(T3[20:16]),
    .Read_Data_1(T2), .Read_Data_2(WriteData));
  ALU_Control alu_control_1 (.ALUOp(ALUOp), .Func(Func), .Op(alu_control_1_op), .Jr(Jr));
  Multiplexer #(.enable("false"), .width(32)) multiplexer_7 (
    .in0(WriteData), .in1({{17{T1[31]}}, T1[14:6], Func}), .out(multiplexer_7_out), .sel(ALUSrc));
  ALU alu_1 (.A(T2), .B(multiplexer_7_out), .AluOp(alu_control_1_op), .Zero(Zero), .ALUresult(alu_1_aluresult));
  not not_2 (not_2_out, Reloj);
  and and_3 (and_3_out, not_2_out, MemWrite);
  RAM #(.addrWidth(24), .dataWidth(32), .trigger("high")) ram_1 (
    .addr(alu_1_aluresult[23:0]), .we(and_3_out), .oe(MemRead), .din(WriteData), .dout(ram_1_dout));
  Multiplexer #(.enable("false"), .width(32)) multiplexer_8 (
    .in0(alu_1_aluresult), .in1(ram_1_dout), .out(RegWriteData), .sel(MemToReg));

  // Other names for the same wires on the sheet: Reset = in_1; T1 (some bits) = {{16{T1[31]}}, Func};
  //   T3 (some bits) = {{6{T3[31]}}, T1[31], T1[14:6], Func}
endmodule

module Reg_File (
  input  [4:0] Read_Register_1,
  input  RegWrite,
  input  [4:0] Write_Reg,
  input  [31:0] Write_Data,
  input  Clock,
  input  Reset,
  input  [4:0] Read_Register_2,
  output [31:0] Read_Data_1,
  output [31:0] Read_Data_2
);

  wire decoder_1_out0, decoder_1_out1, decoder_1_out2, decoder_1_out3, decoder_1_out4, decoder_1_out5,
       decoder_1_out6, decoder_1_out7, decoder_1_out8, decoder_1_out9, decoder_1_out10, decoder_1_out11,
       decoder_1_out12, decoder_1_out13, decoder_1_out14, decoder_1_out15, decoder_1_out16, decoder_1_out17,
       decoder_1_out18, decoder_1_out19, decoder_1_out20, decoder_1_out21, decoder_1_out22, decoder_1_out23,
       decoder_1_out24, decoder_1_out25, decoder_1_out26, decoder_1_out27, decoder_1_out28, decoder_1_out29,
       decoder_1_out30, decoder_1_out31;
  wire [31:0] register_1_q, register_2_q, register_3_q, register_4_q, register_5_q, register_6_q,
       register_7_q, register_8_q, register_9_q, register_10_q, register_11_q, register_12_q, register_13_q,
       register_14_q, register_15_q, register_16_q, register_17_q, register_18_q, register_19_q,
       register_20_q, register_21_q, register_22_q, register_23_q, register_24_q, register_25_q,
       register_26_q, register_27_q, register_28_q, register_29_q, register_30_q, register_31_q,
       register_32_q;

  Decoder #(.select(5)) decoder_1 (
    .out0(decoder_1_out0), .out1(decoder_1_out1), .out2(decoder_1_out2), .out3(decoder_1_out3),
    .out4(decoder_1_out4), .out5(decoder_1_out5), .out6(decoder_1_out6), .out7(decoder_1_out7),
    .out8(decoder_1_out8), .out9(decoder_1_out9), .out10(decoder_1_out10), .out11(decoder_1_out11),
    .out12(decoder_1_out12), .out13(decoder_1_out13), .out14(decoder_1_out14), .out15(decoder_1_out15),
    .out16(decoder_1_out16), .out17(decoder_1_out17), .out18(decoder_1_out18), .out19(decoder_1_out19),
    .out20(decoder_1_out20), .out21(decoder_1_out21), .out22(decoder_1_out22), .out23(decoder_1_out23),
    .out24(decoder_1_out24), .out25(decoder_1_out25), .out26(decoder_1_out26), .out27(decoder_1_out27),
    .out28(decoder_1_out28), .out29(decoder_1_out29), .out30(decoder_1_out30), .out31(decoder_1_out31),
    .sel(Write_Reg), .en(RegWrite));
  Register #(.width(32)) register_1 (.D({32{1'b0}}), .en(decoder_1_out0), .clk(Clock), .Q(register_1_q), .clr(Reset));
  Register #(.width(32)) register_2 (.D(Write_Data), .en(decoder_1_out1), .clk(Clock), .Q(register_2_q), .clr(Reset));
  Register #(.width(32)) register_3 (.D(Write_Data), .en(decoder_1_out2), .clk(Clock), .Q(register_3_q), .clr(Reset));
  Register #(.width(32)) register_4 (.D(Write_Data), .en(decoder_1_out3), .clk(Clock), .Q(register_4_q), .clr(Reset));
  Register #(.width(32)) register_5 (.D(Write_Data), .en(decoder_1_out4), .clk(Clock), .Q(register_5_q));  // open: clr
  Register #(.width(32)) register_6 (.D(Write_Data), .en(decoder_1_out5), .clk(Clock), .Q(register_6_q), .clr(Reset));
  Register #(.width(32)) register_7 (.D(Write_Data), .en(decoder_1_out6), .clk(Clock), .Q(register_7_q), .clr(Reset));
  Register #(.width(32)) register_8 (.D(Write_Data), .en(decoder_1_out7), .clk(Clock), .Q(register_8_q), .clr(Reset));
  Register #(.width(32)) register_9 (.D(Write_Data), .en(decoder_1_out8), .clk(Clock), .Q(register_9_q), .clr(Reset));
  Register #(.width(32)) register_10 (.D(Write_Data), .en(decoder_1_out9), .clk(Clock), .Q(register_10_q), .clr(Reset));
  Register #(.width(32)) register_11 (
    .D(Write_Data), .en(decoder_1_out10), .clk(Clock), .Q(register_11_q), .clr(Reset));
  Register #(.width(32)) register_12 (
    .D(Write_Data), .en(decoder_1_out11), .clk(Clock), .Q(register_12_q), .clr(Reset));
  Register #(.width(32)) register_13 (
    .D(Write_Data), .en(decoder_1_out12), .clk(Clock), .Q(register_13_q), .clr(Reset));
  Register #(.width(32)) register_14 (
    .D(Write_Data), .en(decoder_1_out13), .clk(Clock), .Q(register_14_q), .clr(Reset));
  Register #(.width(32)) register_15 (
    .D(Write_Data), .en(decoder_1_out14), .clk(Clock), .Q(register_15_q), .clr(Reset));
  Register #(.width(32)) register_16 (
    .D(Write_Data), .en(decoder_1_out15), .clk(Clock), .Q(register_16_q), .clr(Reset));
  Register #(.width(32)) register_17 (
    .D(Write_Data), .en(decoder_1_out16), .clk(Clock), .Q(register_17_q), .clr(Reset));
  Register #(.width(32)) register_18 (
    .D(Write_Data), .en(decoder_1_out17), .clk(Clock), .Q(register_18_q), .clr(Reset));
  Register #(.width(32)) register_19 (
    .D(Write_Data), .en(decoder_1_out18), .clk(Clock), .Q(register_19_q), .clr(Reset));
  Register #(.width(32)) register_20 (
    .D(Write_Data), .en(decoder_1_out19), .clk(Clock), .Q(register_20_q), .clr(Reset));
  Register #(.width(32)) register_21 (
    .D(Write_Data), .en(decoder_1_out20), .clk(Clock), .Q(register_21_q), .clr(Reset));
  Register #(.width(32)) register_22 (
    .D(Write_Data), .en(decoder_1_out21), .clk(Clock), .Q(register_22_q), .clr(Reset));
  Register #(.width(32)) register_23 (
    .D(Write_Data), .en(decoder_1_out22), .clk(Clock), .Q(register_23_q), .clr(Reset));
  Register #(.width(32)) register_24 (
    .D(Write_Data), .en(decoder_1_out23), .clk(Clock), .Q(register_24_q), .clr(Reset));
  Register #(.width(32)) register_25 (
    .D(Write_Data), .en(decoder_1_out24), .clk(Clock), .Q(register_25_q), .clr(Reset));
  Register #(.width(32)) register_26 (
    .D(Write_Data), .en(decoder_1_out25), .clk(Clock), .Q(register_26_q), .clr(Reset));
  Register #(.width(32)) register_27 (
    .D(Write_Data), .en(decoder_1_out26), .clk(Clock), .Q(register_27_q), .clr(Reset));
  Register #(.width(32)) register_28 (
    .D(Write_Data), .en(decoder_1_out27), .clk(Clock), .Q(register_28_q), .clr(Reset));
  Register #(.width(32)) register_29 (
    .D(Write_Data), .en(decoder_1_out28), .clk(Clock), .Q(register_29_q), .clr(Reset));
  Register #(.width(32)) register_30 (
    .D(Write_Data), .en(decoder_1_out29), .clk(Clock), .Q(register_30_q), .clr(Reset));
  Register #(.width(32)) register_31 (
    .D(Write_Data), .en(decoder_1_out30), .clk(Clock), .Q(register_31_q), .clr(Reset));
  Register #(.width(32)) register_32 (
    .D(Write_Data), .en(decoder_1_out31), .clk(Clock), .Q(register_32_q), .clr(Reset));
  Multiplexer #(.enable("false"), .select(5), .width(32)) multiplexer_1 (
    .in0(register_1_q), .in1(register_2_q), .in2(register_3_q), .in3(register_4_q), .in4(register_5_q),
    .in5(register_6_q), .in6(register_7_q), .in7(register_8_q), .in8(register_9_q), .in9(register_10_q),
    .in10(register_11_q), .in11(register_12_q), .in12(register_13_q), .in13(register_14_q),
    .in14(register_15_q), .in15(register_16_q), .in16(register_17_q), .in17(register_18_q),
    .in18(register_19_q), .in19(register_20_q), .in20(register_21_q), .in21(register_22_q),
    .in22(register_23_q), .in23(register_24_q), .in24(register_25_q), .in25(register_26_q),
    .in26(register_27_q), .in27(register_28_q), .in28(register_29_q), .in29(register_30_q),
    .in30(register_31_q), .in31(register_32_q), .out(Read_Data_1), .sel(Read_Register_1));
  Multiplexer #(.enable("false"), .select(5), .width(32)) multiplexer_2 (
    .in0(register_1_q), .in1(register_2_q), .in2(register_3_q), .in3(register_4_q), .in4(register_5_q),
    .in5(register_6_q), .in6(register_7_q), .in7(register_8_q), .in8(register_9_q), .in9(register_10_q),
    .in10(register_11_q), .in11(register_12_q), .in12(register_13_q), .in13(register_14_q),
    .in14(register_15_q), .in15(register_16_q), .in16(register_17_q), .in17(register_18_q),
    .in18(register_19_q), .in19(register_20_q), .in20(register_21_q), .in21(register_22_q),
    .in22(register_23_q), .in23(register_24_q), .in24(register_25_q), .in25(register_26_q),
    .in26(register_27_q), .in27(register_28_q), .in28(register_29_q), .in29(register_30_q),
    .in30(register_31_q), .in31(register_32_q), .out(Read_Data_2), .sel(Read_Register_2));

  // Other names for the same wires on the sheet: WD[31:0] = Write_Data
endmodule

module FA_1bit (
  input  A,
  input  B,
  input  Cin,
  output Cout,
  output S
);

  wire and_1_out, and_2_out, and_3_out, and_4_out, and_5_out, and_6_out, and_7_out, not_1_out, not_2_out,
       not_3_out;

  not not_1 (not_1_out, A);
  not not_2 (not_2_out, B);
  not not_3 (not_3_out, Cin);
  and and_1 (and_1_out, B, Cin);
  and and_2 (and_2_out, A, Cin);
  or or_1 (Cout, and_1_out, and_2_out, and_3_out);
  and and_3 (and_3_out, A, B);
  and and_4 (and_4_out, not_1_out, not_2_out, Cin);
  and and_5 (and_5_out, not_1_out, B, not_3_out);
  and and_6 (and_6_out, A, not_2_out, not_3_out);
  and and_7 (and_7_out, A, B, Cin);
  or or_2 (S, and_4_out, and_5_out, and_6_out, and_7_out);
endmodule

module ALU_1bit (
  input  A,
  input  B,
  input  Cin,
  input  [3:0] control,
  output R,
  output Cout
);

  wire Aopr, Bopr, multiplexer_3_out, not_1_out, not_2_out, Reg_AND, Reg_OR, S;

  not not_1 (not_1_out, B);
  not not_2 (not_2_out, A);
  Multiplexer #(.enable("false")) multiplexer_1 (.in0(B), .in1(not_1_out), .out(Bopr), .sel(control[0]));
  Multiplexer #(.enable("false")) multiplexer_2 (.in0(A), .in1(not_2_out), .out(Aopr), .sel(control[1]));
  and and_1 (Reg_AND, Aopr, Bopr);
  or or_1 (Reg_OR, Aopr, Bopr);
  FA_1bit fa_1bit_1 (.A(Aopr), .B(Bopr), .Cin(Cin), .Cout(Cout), .S(S));
  Multiplexer #(.enable("false")) multiplexer_3 (
    .in0(Reg_AND), .in1(Reg_OR), .out(multiplexer_3_out), .sel(control[3]));
  Multiplexer #(.enable("false")) multiplexer_4 (.in0(multiplexer_3_out), .in1(S), .out(R), .sel(control[2]));
endmodule

module ALU (
  input  [31:0] A,
  input  [31:0] B,
  input  [2:0] AluOp,
  output Zero,
  output [31:0] ALUresult
);

  wire alu_1bit_1_cout, alu_1bit_2_cout, alu_1bit_3_cout, alu_1bit_4_cout, alu_1bit_5_cout, alu_1bit_6_cout,
       alu_1bit_7_cout, alu_1bit_8_cout, alu_1bit_9_cout, alu_1bit_10_cout, alu_1bit_11_cout,
       alu_1bit_12_cout, alu_1bit_13_cout, alu_1bit_14_cout, alu_1bit_15_cout, alu_1bit_16_cout,
       alu_1bit_17_cout, alu_1bit_18_cout, alu_1bit_19_cout, alu_1bit_20_cout, alu_1bit_21_cout,
       alu_1bit_22_cout, alu_1bit_23_cout, alu_1bit_24_cout, alu_1bit_25_cout, alu_1bit_26_cout,
       alu_1bit_27_cout, alu_1bit_28_cout, alu_1bit_29_cout, alu_1bit_30_cout, and_1_out, and_2_out,
       and_3_out, and_4_out, Cin, Control4, Count, not_1_out, or_2_out, Signo;
  wire [3:0] Control;
  wire [31:0] R;

  not not_1 (not_1_out, Cin);
  and and_1 (and_1_out, Count, not_1_out);
  and and_2 (and_2_out, R[31], Count);
  and and_3 (and_3_out, R[31], not_1_out);
  or or_1 (Signo, and_1_out, and_2_out, and_3_out);
  Alu_Con_1bit alu_con_1bit_1 (.ALUOper(AluOp), .Control(Control), .Control4(Control4));
  Multiplexer #(.enable("false"), .width(32)) multiplexer_1 (
    .in0(R), .in1({{31{1'b0}}, Signo}), .out(ALUresult), .sel(Control4));
  or or_2 (or_2_out, R[0], R[1], R[2], R[3], R[4], R[5], R[6], R[7], R[8], R[9], R[10], R[11], R[12], R[13], R[14], R[15], R[16], R[17], R[18], R[19], R[20], R[21], R[22], R[23], R[24], R[25], R[26], R[27], R[28], R[29], R[30], R[31]);
  not not_2 (Zero, or_2_out);
  and and_4 (and_4_out, Control[0], Control[2]);
  ALU_1bit alu_1bit_1 (.A(A[0]), .B(B[0]), .Cin(and_4_out), .control(Control), .R(R[0]), .Cout(alu_1bit_1_cout));
  ALU_1bit alu_1bit_2 (
    .A(A[1]), .Cin(alu_1bit_1_cout), .control(Control), .R(R[1]), .Cout(alu_1bit_2_cout));  // open: B
  ALU_1bit alu_1bit_3 (.A(A[2]), .B(B[2]), .Cin(alu_1bit_2_cout), .control(Control), .R(R[2]), .Cout(alu_1bit_3_cout));
  ALU_1bit alu_1bit_4 (.A(A[3]), .B(B[3]), .Cin(alu_1bit_3_cout), .control(Control), .R(R[3]), .Cout(alu_1bit_4_cout));
  ALU_1bit alu_1bit_5 (.A(A[4]), .B(B[4]), .Cin(alu_1bit_4_cout), .control(Control), .R(R[4]), .Cout(alu_1bit_5_cout));
  ALU_1bit alu_1bit_6 (.A(A[5]), .B(B[5]), .Cin(alu_1bit_5_cout), .control(Control), .R(R[5]), .Cout(alu_1bit_6_cout));
  ALU_1bit alu_1bit_7 (.A(A[6]), .B(B[6]), .Cin(alu_1bit_6_cout), .control(Control), .R(R[6]), .Cout(alu_1bit_7_cout));
  ALU_1bit alu_1bit_8 (.A(A[7]), .B(B[7]), .Cin(alu_1bit_7_cout), .control(Control), .R(R[7]), .Cout(alu_1bit_8_cout));
  ALU_1bit alu_1bit_9 (
    .A(A[8]), .Cin(alu_1bit_8_cout), .control(Control), .R(R[8]), .Cout(alu_1bit_9_cout));  // open: B
  ALU_1bit alu_1bit_10 (
    .A(A[9]), .Cin(alu_1bit_9_cout), .control(Control), .R(R[9]), .Cout(alu_1bit_10_cout));  // open: B
  ALU_1bit alu_1bit_11 (
    .A(A[10]), .B(B[10]), .Cin(alu_1bit_10_cout), .control(Control), .R(R[10]), .Cout(alu_1bit_11_cout));
  ALU_1bit alu_1bit_12 (
    .A(A[11]), .B(B[11]), .Cin(alu_1bit_11_cout), .control(Control), .R(R[11]), .Cout(alu_1bit_12_cout));
  ALU_1bit alu_1bit_13 (
    .A(A[12]), .B(B[12]), .Cin(alu_1bit_12_cout), .control(Control), .R(R[12]), .Cout(alu_1bit_13_cout));
  ALU_1bit alu_1bit_14 (
    .A(A[13]), .B(B[13]), .Cin(alu_1bit_13_cout), .control(Control), .R(R[13]), .Cout(alu_1bit_14_cout));
  ALU_1bit alu_1bit_15 (
    .A(A[14]), .B(B[14]), .Cin(alu_1bit_14_cout), .control(Control), .R(R[14]), .Cout(alu_1bit_15_cout));
  ALU_1bit alu_1bit_16 (
    .A(A[15]), .B(B[15]), .Cin(alu_1bit_15_cout), .control(Control), .R(R[15]), .Cout(alu_1bit_16_cout));
  ALU_1bit alu_1bit_17 (
    .A(A[16]), .B(B[16]), .Cin(alu_1bit_16_cout), .control(Control), .R(R[16]), .Cout(alu_1bit_17_cout));
  ALU_1bit alu_1bit_18 (
    .A(A[17]), .B(B[17]), .Cin(alu_1bit_17_cout), .control(Control), .R(R[17]), .Cout(alu_1bit_18_cout));
  ALU_1bit alu_1bit_19 (
    .A(A[18]), .B(B[18]), .Cin(alu_1bit_18_cout), .control(Control), .R(R[18]), .Cout(alu_1bit_19_cout));
  ALU_1bit alu_1bit_20 (
    .A(A[19]), .B(B[19]), .Cin(alu_1bit_19_cout), .control(Control), .R(R[19]), .Cout(alu_1bit_20_cout));
  ALU_1bit alu_1bit_21 (
    .A(A[20]), .B(B[20]), .Cin(alu_1bit_20_cout), .control(Control), .R(R[20]), .Cout(alu_1bit_21_cout));
  ALU_1bit alu_1bit_22 (
    .A(A[21]), .B(B[21]), .Cin(alu_1bit_21_cout), .control(Control), .R(R[21]), .Cout(alu_1bit_22_cout));
  ALU_1bit alu_1bit_23 (
    .A(A[22]), .B(B[22]), .Cin(alu_1bit_22_cout), .control(Control), .R(R[22]), .Cout(alu_1bit_23_cout));
  ALU_1bit alu_1bit_24 (
    .A(A[23]), .B(B[23]), .Cin(alu_1bit_23_cout), .control(Control), .R(R[23]), .Cout(alu_1bit_24_cout));
  ALU_1bit alu_1bit_25 (
    .A(A[24]), .B(B[24]), .Cin(alu_1bit_24_cout), .control(Control), .R(R[24]), .Cout(alu_1bit_25_cout));
  ALU_1bit alu_1bit_26 (
    .A(A[25]), .B(B[25]), .Cin(alu_1bit_25_cout), .control(Control), .R(R[25]), .Cout(alu_1bit_26_cout));
  ALU_1bit alu_1bit_27 (
    .A(A[26]), .B(B[26]), .Cin(alu_1bit_26_cout), .control(Control), .R(R[26]), .Cout(alu_1bit_27_cout));
  ALU_1bit alu_1bit_28 (
    .A(A[27]), .B(B[27]), .Cin(alu_1bit_27_cout), .control(Control), .R(R[27]), .Cout(alu_1bit_28_cout));
  ALU_1bit alu_1bit_29 (
    .A(A[28]), .B(B[28]), .Cin(alu_1bit_28_cout), .control(Control), .R(R[28]), .Cout(alu_1bit_29_cout));
  ALU_1bit alu_1bit_30 (
    .A(A[29]), .B(B[29]), .Cin(alu_1bit_29_cout), .control(Control), .R(R[29]), .Cout(alu_1bit_30_cout));
  ALU_1bit alu_1bit_31 (.A(A[30]), .B(B[30]), .Cin(alu_1bit_30_cout), .control(Control), .R(R[30]), .Cout(Cin));
  ALU_1bit alu_1bit_32 (.A(A[31]), .B(B[31]), .Cin(Cin), .control(Control), .R(R[31]), .Cout(Count));
endmodule

module ALU_Control (
  input  [1:0] ALUOp,
  input  [5:0] Func,
  output [2:0] Op,
  output Jr
);

  wire alu_co_1_jr;
  wire [2:0] alu_co_1_aluoper;
  wire [2:2] not_1_out;

  not not_1 (not_1_out[2], ALUOp[0]);
  ALU_CO alu_co_1 (.Func(Func), .Jr(alu_co_1_jr), .ALUOper(alu_co_1_aluoper));
  Multiplexer #(.enable("false"), .width(3)) multiplexer_1 (
    .in0({not_1_out[2], ALUOp[0], 1'b1}), .in1(alu_co_1_aluoper), .out(Op), .sel(ALUOp[1]));
  and and_1 (Jr, alu_co_1_jr, ALUOp[1]);

  // Other names for the same wires on the sheet: F = ALUOp[1]
endmodule

module ALU_CO (
  input  [5:0] Func,
  output Jr,
  output [2:0] ALUOper
);

  wire and_2_out, and_3_out, and_4_out, and_5_out, and_6_out, and_7_out, and_8_out, not_1_out, not_2_out,
       not_3_out, not_4_out, not_5_out, not_6_out;

  not not_1 (not_1_out, Func[5]);
  not not_2 (not_2_out, Func[4]);
  not not_3 (not_3_out, Func[3]);
  not not_4 (not_4_out, Func[2]);
  not not_5 (not_5_out, Func[1]);
  not not_6 (not_6_out, Func[0]);
  and and_1 (Jr, not_1_out, not_2_out, Func[3], not_4_out, not_5_out, not_6_out);
  and and_2 (and_2_out, Func[5], not_2_out, not_3_out, not_4_out, not_5_out, not_6_out);
  and and_3 (and_3_out, Func[5], not_2_out, not_3_out, Func[2], Func[1], Func[0]);
  and and_4 (and_4_out, Func[5], not_2_out, Func[3], not_4_out, Func[1], not_6_out);
  and and_5 (and_5_out, Func[5], not_2_out, not_3_out, Func[2], not_5_out);
  and and_6 (and_6_out, Func[5], not_2_out, not_3_out, Func[2], Func[0]);
  and and_7 (and_7_out, Func[5], not_2_out, not_3_out, not_4_out, not_6_out);
  and and_8 (and_8_out, Func[5], not_2_out, not_3_out, Func[2], Func[0]);
  or or_1 (ALUOper[2], and_2_out, and_3_out, and_4_out);
  or or_2 (ALUOper[1], and_5_out, and_6_out);
  or or_3 (ALUOper[0], and_7_out, and_8_out);
endmodule

module Alu_Con_Op (
  input  [5:0] Opcode,
  output salir,
  output RegDest,
  output Jump,
  output ALUSrc,
  output MemtonReg,
  output RegWrite,
  output MemRead,
  output MemWrite,
  output Branch,
  output Jal,
  output [1:0] ALUOp
);

  wire and_2_out, and_3_out, and_7_out, and_8_out, and_13_out, and_14_out, not_1_out, not_2_out, not_3_out,
       not_4_out, not_5_out, not_6_out;

  not not_1 (not_1_out, Opcode[5]);
  not not_2 (not_2_out, Opcode[4]);
  not not_3 (not_3_out, Opcode[3]);
  not not_4 (not_4_out, Opcode[2]);
  not not_5 (not_5_out, Opcode[1]);
  not not_6 (not_6_out, Opcode[0]);
  and and_1 (salir, Opcode[5], Opcode[4], Opcode[3], Opcode[2], Opcode[1], Opcode[0]);
  and and_2 (and_2_out, not_1_out, not_2_out, not_3_out, not_5_out, not_6_out);
  and and_3 (and_3_out, not_1_out, not_2_out, not_3_out, not_4_out, Opcode[1]);
  and and_4 (Jump, not_1_out, not_2_out, not_3_out, not_4_out, Opcode[1]);
  and and_5 (ALUSrc, Opcode[5], not_2_out, not_4_out, Opcode[1], Opcode[0]);
  and and_6 (MemtonReg, Opcode[5], not_2_out, not_4_out, Opcode[1], Opcode[0]);
  and and_7 (and_7_out, not_1_out, not_2_out, not_3_out, not_4_out, not_5_out, not_6_out);
  and and_8 (and_8_out, not_2_out, not_3_out, not_4_out, Opcode[1], Opcode[0]);
  and and_9 (MemRead, not_2_out, not_3_out, not_4_out, Opcode[1], Opcode[0]);
  and and_10 (MemWrite, Opcode[5], not_2_out, Opcode[3], not_4_out, Opcode[1], Opcode[0]);
  and and_11 (Branch, not_1_out, not_2_out, not_3_out, Opcode[2], not_5_out, not_6_out);
  and and_12 (Jal, not_1_out, not_2_out, not_3_out, not_4_out, Opcode[1]);
  and and_13 (and_13_out, not_1_out, not_2_out, not_3_out, Opcode[2], not_5_out, not_6_out);
  and and_14 (and_14_out, Opcode[5], not_2_out, not_4_out, Opcode[1], Opcode[0]);
  and and_15 (ALUOp[0], Opcode[5], not_2_out, not_4_out, Opcode[1], Opcode[0]);
  or or_1 (RegDest, and_2_out, and_3_out);
  or or_2 (RegWrite, and_7_out, and_8_out);
  or or_3 (ALUOp[1], and_13_out, and_14_out);
endmodule

module Alu_Con_1bit (
  input  [2:0] ALUOper,
  output [3:0] Control,
  output Control4
);

  wire and_2_out, and_3_out, and_5_out, and_6_out, not_1_out, not_2_out, not_3_out;

  not not_1 (not_1_out, ALUOper[2]);
  not not_2 (not_2_out, ALUOper[1]);
  not not_3 (not_3_out, ALUOper[0]);
  and and_1 (Control[3], not_2_out, ALUOper[0]);
  and and_2 (and_2_out, ALUOper[2], not_2_out);
  and and_3 (and_3_out, ALUOper[2], not_3_out);
  and and_4 (Control[1], not_1_out, not_2_out, not_3_out);
  and and_5 (and_5_out, not_2_out, not_3_out);
  and and_6 (and_6_out, ALUOper[2], not_3_out);
  and and_7 (Control4, ALUOper[2], not_2_out, not_3_out);
  or or_1 (Control[2], and_2_out, and_3_out);
  or or_2 (Control[0], and_5_out, and_6_out);
endmodule
